// Logisim project CSE 331 Section 04 Group 08 Logisim Circuit.circ as structural Verilog: 1 circuit, main circuit main
module main (
  input  I3,
  input  I2,
  input  I1,
  input  I0,
  output O3,
  output O2,
  output O1,
  output O0
);

  wire and_1_out, and_2_out, and_3_out, and_4_out, and_5_out, and_6_out, and_7_out, and_8_out, and_9_out,
       and_10_out, and_11_out, and_12_out, and_13_out, and_14_out, and_15_out, and_16_out, and_17_out,
       and_18_out, not_1_out, not_2_out, not_3_out, not_4_out;

  not not_1 (not_1_out, I3);
  not not_2 (not_2_out, I2);
  not not_3 (not_3_out, I1);
  not not_4 (not_4_out, I0);
  and and_1 (and_1_out, not_3_out, not_2_out, I3);
  and and_2 (and_2_out, not_4_out, I1, not_1_out);
  and and_3 (and_3_out, I0, not_3_out, not_2_out);
  and and_4 (and_4_out, I0, not_3_out, I3);
  and and_5 (and_5_out, not_3_out, I2, not_1_out);
  and and_6 (and_6_out, not_4_out, I1, not_2_out);
  and and_7 (and_7_out, I0, not_3_out, I3);
  and and_8 (and_8_out, I0, I2, not_1_out);
  and and_9 (and_9_out, not_4_out, not_3_out, not_2_out);
  and and_10 (and_10_out, not_3_out, I2, I3);
  and and_11 (and_11_out, I0, I1, not_1_out);
  and and_12 (and_12_out, not_3_out, not_2_out, not_1_out);
  and and_13 (and_13_out, I0, I1, I2);
  and and_14 (and_14_out, not_4_out, not_3_out, I3);
  and and_15 (and_15_out, not_4_out, I1, not_2_out);
  and and_16 (and_16_out, I1, I2, not_1_out);
  and and_17 (and_17_out, I0, not_3_out, I2);
  and and_18 (and_18_out, I1, not_2_out, I3);
  or or_1 (O0, and_1_out, and_2_out, and_3_out, and_4_out);
  or or_2 (O1, and_5_out, and_6_out, and_7_out, and_8_out);
  or or_3 (O2, and_9_out, and_10_out, and_11_out, and_12_out, and_13_out);
  or or_4 (O3, and_14_out, and_15_out, and_16_out, and_17_out, and_18_out);
endmodule
